// Logisim project ALU_74381.circ as structural Verilog: 1 circuit, main circuit alu_74381_lib
module alu_74381_lib (
  input  Cn,
  input  A0,
  input  A1,
  input  A2,
  input  A3,
  input  B0,
  input  B1,
  input  B2,
  input  B3,
  input  S0,
  input  S1,
  input  S2,
  output nP,
  output nG,
  output F0,
  output F1,
  output F2,
  output F3
);

  // _74381 #(.ShowInternalStructure("true")) 74381_1: pin names not known; wires that end beside it: A1, A2, B1, B2, A0, A3, B0, B3, S0, Cn, S1, nP, S2, nG, F0, F3, F1, F2
  LED LCi (.in(Cn));
  LED #(.active("false")) Lnp (.in(nP));
  LED #(.active("false")) Lng (.in(nG));
endmodule
