// Logisim project REG4b_lib.circ as structural Verilog: 1 circuit, main circuit REG4_lib
module REG4_lib (
  input  in_1,
  input  in_2,
  input  in_3,
  input  in_4,
  input  in_5,
  output out_6,
  output out_7,
  output out_8,
  output out_9
);

  // Probe on {out_9, out_8, out_7, out_6}
  Register #(.width(4)) register_1 (
    .D({in_4, in_3, in_2, in_1}), .clk(in_5), .Q({out_9, out_8, out_7, out_6}));  // open: en, clr
endmodule
