// Logisim project ST_8_lib.circ as structural Verilog: 1 circuit, main circuit ST_8_lib
module ST_8_lib (
  input  R,
  input  LD,
  input  C,
  input  D0,
  input  D1,
  input  D2,
  input  D3,
  input  D4,
  input  D5,
  input  D6,
  input  D7,
  output Q0,
  output Q1,
  output Q2,
  output Q3,
  output Q4,
  output Q5,
  output Q6,
  output Q7
);

  Counter counter_1 (
    .clr(R), .load(LD), .clk(C), .D({D7, D6, D5, D4, D3, D2, D1, D0}), .Q({Q7, Q6, Q5, Q4, Q3, Q2, Q1, Q0}));  // open: up, count, carry
endmodule
