// Logisim project lab1.circ as structural Verilog: 6 circuits, main circuit part_1
module part_1 (
  input  LD_A,
  input  LD_OUT,
  input  [3:0] D3_D0,
  input  LD_B,
  input  Cn,
  input  S2,
  input  S1,
  input  S0
);

  wire [3:0] alu_74381_lib_1_f0, RegA_out_6, RegB_out_6, RegOUT_out_6;

  Hex_Digit_Display hex_digit_display_1 (.value(D3_D0));  // open: dp
  // Probe on D3_D0
  REG4_lib RegA (
    .in_5(LD_A), .in_1(alu_74381_lib_1_f0[0]), .in_2(alu_74381_lib_1_f0[1]), .in_3(alu_74381_lib_1_f0[2]),
    .in_4(alu_74381_lib_1_f0[3]), .out_6(RegA_out_6[0]), .out_7(RegA_out_6[1]), .out_8(RegA_out_6[2]),
    .out_9(RegA_out_6[3]));
  REG4_lib RegB (
    .in_5(LD_B), .in_1(D3_D0[0]), .in_2(D3_D0[1]), .in_3(D3_D0[2]), .in_4(D3_D0[3]), .out_6(RegB_out_6[0]),
    .out_7(RegB_out_6[1]), .out_8(RegB_out_6[2]), .out_9(RegB_out_6[3]));
  Hex_Digit_Display hex_digit_display_2 (.value(RegA_out_6));  // open: dp
  // Probe on RegA_out_6
  Hex_Digit_Display hex_digit_display_3 (.value(RegB_out_6));  // open: dp
  // Probe on RegB_out_6
  REG4_lib RegOUT (
    .in_5(LD_OUT), .in_1(RegA_out_6[0]), .in_2(RegA_out_6[1]), .in_3(RegA_out_6[2]), .in_4(RegA_out_6[3]),
    .out_6(RegOUT_out_6[0]), .out_7(RegOUT_out_6[1]), .out_8(RegOUT_out_6[2]), .out_9(RegOUT_out_6[3]));
  Hex_Digit_Display hex_digit_display_4 (.value(RegOUT_out_6));  // open: dp
  // Probe on RegOUT_out_6
  alu_74381_lib alu_74381_lib_1 (
    .Cn(Cn), .A0(RegA_out_6[0]), .A1(RegA_out_6[1]), .A2(RegA_out_6[2]), .A3(RegA_out_6[3]),
    .B0(RegB_out_6[0]), .B1(RegB_out_6[1]), .B2(RegB_out_6[2]), .B3(RegB_out_6[3]), .S0(S0), .S1(S1),
    .S2(S2), .F0(alu_74381_lib_1_f0[0]), .F1(alu_74381_lib_1_f0[1]), .F2(alu_74381_lib_1_f0[2]),
    .F3(alu_74381_lib_1_f0[3]));  // open: nP, nG
  Hex_Digit_Display hex_digit_display_5 (.value(alu_74381_lib_1_f0));  // open: dp
  // Probe on alu_74381_lib_1_f0
endmodule

module part_3 (
  input  Clock,
  output LD_B,
  output LD_A,
  output LD_OUT,
  output [3:0] D3_D0,
  output Cn,
  output [2:0] S2_S0
);

  wire and_1_out, not_1_out, not_2_out, not_3_out, not_4_out, not_5_out, not_6_out, not_7_out, not_8_out,
       not_9_out, not_10_out, not_11_out, not_12_out, not_13_out, not_14_out, not_15_out, or_1_out, Reset_out;
  wire [7:0] st_8_lib1_1_q0;
  wire [15:0] rom_1_data;

  Button Reset (.out(Reset_out));
  not not_1 (not_1_out, Clock);
  or or_1 (or_1_out, Reset_out, and_1_out);
  and and_1 (and_1_out, st_8_lib1_1_q0[1], st_8_lib1_1_q0[2], st_8_lib1_1_q0[5]);
  ST_8_lib1 st_8_lib1_1 (
    .R(or_1_out), .C(not_1_out), .Q0(st_8_lib1_1_q0[0]), .Q1(st_8_lib1_1_q0[1]), .Q2(st_8_lib1_1_q0[2]),
    .Q3(st_8_lib1_1_q0[3]), .Q4(st_8_lib1_1_q0[4]), .Q5(st_8_lib1_1_q0[5]), .Q6(st_8_lib1_1_q0[6]),
    .Q7(st_8_lib1_1_q0[7]));  // open: LD, D0, D1, D2, D3, D4, D5, D6, D7
  // Probe on st_8_lib1_1_q0
  ROM #(.dataWidth(16), .misaligned("true")) rom_1 (
    .addr(st_8_lib1_1_q0),
    .data({rom_1_data[15], S2_S0, rom_1_data[11], Cn, rom_1_data[9:8], D3_D0, rom_1_data[3:0]}));
  and and_2 (LD_B, Clock, not_2_out);
  not not_2 (not_2_out, not_3_out);
  not not_3 (not_3_out, not_4_out);
  not not_4 (not_4_out, not_5_out);
  not not_5 (not_5_out, not_6_out);
  not not_6 (not_6_out, rom_1_data[1]);
  and and_3 (LD_A, Clock, not_7_out);
  not not_7 (not_7_out, not_8_out);
  not not_8 (not_8_out, not_9_out);
  not not_9 (not_9_out, not_10_out);
  not not_10 (not_10_out, not_11_out);
  not not_11 (not_11_out, rom_1_data[2]);
  and and_4 (LD_OUT, Clock, not_12_out);
  not not_12 (not_12_out, not_13_out);
  not not_13 (not_13_out, not_14_out);
  not not_14 (not_14_out, not_15_out);
  not not_15 (not_15_out, rom_1_data[0]);

  // Notes on the sheet:
  //   contents of rom_1 (hex, n*v repeats v):
  //   6 2 14 f0f0
endmodule

module part_4 (
  input  Clock
);

  wire and_1_out, Cn, LD_A, LD_B, LD_OUT, not_1_out, not_2_out, not_3_out, not_4_out, not_5_out, not_6_out,
       not_7_out, not_8_out, not_9_out, not_10_out, not_11_out, not_12_out, not_13_out, not_14_out,
       not_15_out, or_1_out, Reset_out;
  wire [2:0] S2_S0;
  wire [3:0] alu_74381_lib_1_f0, D3_D0, RegA_out_6, RegB_out_6, RegOUT_out_6;
  wire [7:0] st_8_lib1_1_q0;
  wire [15:0] rom_1_data;

  Button Reset (.out(Reset_out));
  Hex_Digit_Display hex_digit_display_1 (.value(D3_D0));  // open: dp
  // Probe on D3_D0
  not not_1 (not_1_out, Clock);
  or or_1 (or_1_out, Reset_out, and_1_out);
  and and_1 (and_1_out, st_8_lib1_1_q0[1], st_8_lib1_1_q0[2], st_8_lib1_1_q0[5]);
  ST_8_lib1 st_8_lib1_1 (
    .R(or_1_out), .C(not_1_out), .Q0(st_8_lib1_1_q0[0]), .Q1(st_8_lib1_1_q0[1]), .Q2(st_8_lib1_1_q0[2]),
    .Q3(st_8_lib1_1_q0[3]), .Q4(st_8_lib1_1_q0[4]), .Q5(st_8_lib1_1_q0[5]), .Q6(st_8_lib1_1_q0[6]),
    .Q7(st_8_lib1_1_q0[7]));  // open: LD, D0, D1, D2, D3, D4, D5, D6, D7
  REG4_lib RegA (
    .in_5(LD_A), .in_1(alu_74381_lib_1_f0[0]), .in_2(alu_74381_lib_1_f0[1]), .in_3(alu_74381_lib_1_f0[2]),
    .in_4(alu_74381_lib_1_f0[3]), .out_6(RegA_out_6[0]), .out_7(RegA_out_6[1]), .out_8(RegA_out_6[2]),
    .out_9(RegA_out_6[3]));
  Hex_Digit_Display hex_digit_display_2 (.value(RegA_out_6));  // open: dp
  // Probe on RegA_out_6
  REG4_lib RegB (
    .in_5(LD_B), .in_1(D3_D0[0]), .in_2(D3_D0[1]), .in_3(D3_D0[2]), .in_4(D3_D0[3]), .out_6(RegB_out_6[0]),
    .out_7(RegB_out_6[1]), .out_8(RegB_out_6[2]), .out_9(RegB_out_6[3]));
  Hex_Digit_Display hex_digit_display_3 (.value(RegB_out_6));  // open: dp
  // Probe on RegB_out_6
  ROM #(.dataWidth(16), .misaligned("true")) rom_1 (
    .addr(st_8_lib1_1_q0),
    .data({rom_1_data[15], S2_S0, rom_1_data[11], Cn, rom_1_data[9:8], D3_D0, rom_1_data[3:0]}));
  // Probe on st_8_lib1_1_q0
  REG4_lib RegOUT (
    .in_5(LD_OUT), .in_1(RegA_out_6[0]), .in_2(RegA_out_6[1]), .in_3(RegA_out_6[2]), .in_4(RegA_out_6[3]),
    .out_6(RegOUT_out_6[0]), .out_7(RegOUT_out_6[1]), .out_8(RegOUT_out_6[2]), .out_9(RegOUT_out_6[3]));
  Hex_Digit_Display hex_digit_display_4 (.value(RegOUT_out_6));  // open: dp
  // Probe on RegOUT_out_6
  alu_74381_lib alu_74381_lib_1 (
    .Cn(Cn), .A0(RegA_out_6[0]), .A1(RegA_out_6[1]), .A2(RegA_out_6[2]), .A3(RegA_out_6[3]),
    .B0(RegB_out_6[0]), .B1(RegB_out_6[1]), .B2(RegB_out_6[2]), .B3(RegB_out_6[3]), .S0(S2_S0[0]),
    .S1(S2_S0[1]), .S2(S2_S0[2]), .F0(alu_74381_lib_1_f0[0]), .F1(alu_74381_lib_1_f0[1]),
    .F2(alu_74381_lib_1_f0[2]), .F3(alu_74381_lib_1_f0[3]));  // open: nP, nG
  Hex_Digit_Display hex_digit_display_5 (.value(alu_74381_lib_1_f0));  // open: dp
  // Probe on alu_74381_lib_1_f0
  and and_2 (LD_B, Clock, not_2_out);
  not not_2 (not_2_out, not_3_out);
  not not_3 (not_3_out, not_4_out);
  not not_4 (not_4_out, not_5_out);
  not not_5 (not_5_out, not_6_out);
  not not_6 (not_6_out, rom_1_data[1]);
  and and_3 (LD_A, Clock, not_7_out);
  not not_7 (not_7_out, not_8_out);
  not not_8 (not_8_out, not_9_out);
  not not_9 (not_9_out, not_10_out);
  not not_10 (not_10_out, not_11_out);
  not not_11 (not_11_out, rom_1_data[2]);
  and and_4 (LD_OUT, Clock, not_12_out);
  not not_12 (not_12_out, not_13_out);
  not not_13 (not_13_out, not_14_out);
  not not_14 (not_14_out, not_15_out);
  not not_15 (not_15_out, rom_1_data[0]);

  // Notes on the sheet:
  //   contents of rom_1 (hex, n*v repeats v):
  //   6 2 14 3002 7 2 7 34 3002 44 3002 7 4 1402 7 d4 2402 7 24 4002 7 54 3002 7 64 2402 7 4 1402 7 f4
  //   3002 7 74 4002 7 220*6
endmodule

module alu_74381_lib (
  input  Cn,
  input  A0,
  input  A1,
  input  A2,
  input  A3,
  input  B0,
  input  B1,
  input  B2,
  input  B3,
  input  S0,
  input  S1,
  input  S2,
  output nP,
  output nG,
  output F0,
  output F1,
  output F2,
  output F3
);

  // _74381 #(.ShowInternalStructure("true")) 74381_1: pin names not known; wires that end beside it: A1, A2, B1, B2, A0, A3, B0, B3, S0, Cn, S1, nP, S2, nG, F0, F3, F1, F2
  LED LCi (.in(Cn));
  LED #(.active("false")) Lnp (.in(nP));
  LED #(.active("false")) Lng (.in(nG));
endmodule

module REG4_lib (
  input  in_1,
  input  in_2,
  input  in_3,
  input  in_4,
  input  in_5,
  output out_6,
  output out_7,
  output out_8,
  output out_9
);

  // Probe on {out_9, out_8, out_7, out_6}
  Register #(.width(4)) register_1 (
    .D({in_4, in_3, in_2, in_1}), .clk(in_5), .Q({out_9, out_8, out_7, out_6}));  // open: en, clr
endmodule

module ST_8_lib1 (
  input  R,
  input  LD,
  input  C,
  input  D0,
  input  D1,
  input  D2,
  input  D3,
  input  D4,
  input  D5,
  input  D6,
  input  D7,
  output Q0,
  output Q1,
  output Q2,
  output Q3,
  output Q4,
  output Q5,
  output Q6,
  output Q7
);

  Counter counter_1 (
    .clr(R), .load(LD), .clk(C), .D({D7, D6, D5, D4, D3, D2, D1, D0}), .Q({Q7, Q6, Q5, Q4, Q3, Q2, Q1, Q0}));  // open: up, count, carry
endmodule
